# Fritzing sketch mmb_schematic (saved by Fritzing 1.0.0rc)
breadboards: 1

parts:
  Bauteil1 = HX711 Weighing Sensor Module
  Mod1 = Raspberry Pi Pico
  Grove1 = Grove OLED 128x96  # not connected
  S1 = Pushbutton [package="[THT]"]
  S2 = Pushbutton [package="[THT]"]
  Bauteil2 = ws2812b [package="smd 2812b"]

nets:
  N1: Bauteil1.VCC, Mod1.pin_36
  GND: Bauteil1.GND, Mod1.pin_3, Mod1.pin_8, Mod1.pin_13, Mod1.pin_18, Mod1.pin_23, Mod1.pin_28, Mod1.pin_33, Mod1.pin_38, Mod1.pin_42, S1.Pin_1, S1.Pin_2, S2.Pin_1, S2.Pin_2, Bauteil2.VSS
  N2: Mod1.pin_4, S2.Pin_3, S2.Pin_4
  N3: Mod1.pin_29, S1.Pin_3, S1.Pin_4
  N4: Mod1.pin_34, Bauteil2.DIN
  N5: Mod1.pin_40, Bauteil2.VDD

custom parts:
  Raspberry Pi Pico: Raspberry Pi Pico. Based around the RP2040 microcontroller the Pico is a low cost microcontroller device bringing Raspberry Pi quality, cost, and easy of use to the microcontroller space. Jan 2021, Split part in to two versions: tht (this one) and SMD. This one will drill holes for a .1 in header in pcb to allow plugging in the module as well as providing pads to solder the module to the top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
