# Fritzing sketch mmb_schematic_buttons (saved by Fritzing 1.0.0rc)
breadboards: 1

parts:
  Bauteil1 = HX711 Weighing Sensor Module
  Mod1 = Raspberry Pi Pico
  Grove1 = Grove OLED 128x96  # not connected
  S1 = Pushbutton [package="[THT]"]
  S2 = Pushbutton [package="[THT]"]
  Bauteil2 = ws2812b [package="smd 2812b"]
  S3 = Pushbutton [package="[THT]"]
  U1 = Hirose DF13 Series Header [part_number=DF13#-4P-1.25V package=DF13C-4P-1.25V]

nets:
  GND: Bauteil1.GND, Mod1.pin_3, Mod1.pin_8, Mod1.pin_13, Mod1.pin_18, Mod1.pin_23, Mod1.pin_28, Mod1.pin_33, Mod1.pin_38, Mod1.pin_42, S1.Pin_1, S1.Pin_2, S2.Pin_1, S2.Pin_2, Bauteil2.VSS, S3.Pin_1, S3.Pin_2
  N1: Bauteil1.E+, U1.4
  N2: Bauteil1.E-, U1.3
  N3: Bauteil1.A+, U1.2
  N4: Bauteil1.A-, U1.1
  N5: Mod1.pin_4, S2.Pin_3, S2.Pin_4
  N6: Mod1.pin_5, S1.Pin_3, S1.Pin_4
  N7: Mod1.pin_20, S3.Pin_3, S3.Pin_4
  N8: Mod1.pin_34, Bauteil2.DIN
  N9: Mod1.pin_40, Bauteil2.VDD

custom parts:
  Raspberry Pi Pico: Raspberry Pi Pico. Based around the RP2040 microcontroller the Pico is a low cost microcontroller device bringing Raspberry Pi quality, cost, and easy of use to the microcontroller space. Jan 2021, Split part in to two versions: tht (this one) and SMD. This one will drill holes for a .1 in header in pcb to allow plugging in the module as well as providing pads to solder the module to the top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
